// Logisim project sumator4b.circ as structural Verilog: 2 circuits, main circuit main
module main (
  input  a3,
  input  a2,
  input  a1,
  input  a0,
  input  b3,
  input  b2,
  input  b1,
  input  b0,
  output co,
  output s3,
  output s2,
  output s1,
  output s0
);

  wire sumator1b_2_co, sumator1b_3_co, sumator1b_4_co;

  sumator1b sumator1b_1 (.a(a3), .b(b3), .ci(sumator1b_2_co), .co(co), .s(s3));
  sumator1b sumator1b_2 (.a(a2), .b(b2), .ci(sumator1b_3_co), .co(sumator1b_2_co), .s(s2));
  sumator1b sumator1b_3 (.a(a1), .b(b1), .ci(sumator1b_4_co), .co(sumator1b_3_co), .s(s1));
  sumator1b sumator1b_4 (.a(a0), .b(b0), .ci(1'b0), .co(sumator1b_4_co), .s(s0));

  // Notes on the sheet:
  //   Sumator complet pe 4 biţi
endmodule

module sumator1b (
  input  a,
  input  b,
  input  ci,
  output co,
  output s
);

  wire demultiplexer_1_out0, demultiplexer_1_out1, demultiplexer_1_out2, demultiplexer_1_out3,
       demultiplexer_1_out4, demultiplexer_1_out5, demultiplexer_1_out6, demultiplexer_1_out7;

  Demultiplexer #(.select(3), .enable("false")) demultiplexer_1 (
    .out0(demultiplexer_1_out0), .out1(demultiplexer_1_out1), .out2(demultiplexer_1_out2),
    .out3(demultiplexer_1_out3), .out4(demultiplexer_1_out4), .out5(demultiplexer_1_out5),
    .out6(demultiplexer_1_out6), .out7(demultiplexer_1_out7), .in(1'b1), .sel({a, b, ci}));
  or or_1 (co, demultiplexer_1_out3, demultiplexer_1_out5, demultiplexer_1_out6, demultiplexer_1_out7);
  or or_2 (s, demultiplexer_1_out1, demultiplexer_1_out2, demultiplexer_1_out4, demultiplexer_1_out7);
endmodule
