// Logisim project scadere.circ as structural Verilog: 3 circuits, main circuit main
module main (
  input  a3,
  input  a2,
  input  a1,
  input  a0,
  input  Cin,
  input  b3,
  input  b2,
  input  b1,
  input  b0,
  output ov,
  output co,
  output D3,
  output D2,
  output D1,
  output D0
);

  wire not_1_out, not_2_out, not_3_out, not_4_out, sumator1b_2_co, sumator1b_3_co, sumator1b_4_co;

  sumator1b sumator1b_1 (.a(a3), .b(not_1_out), .ci(sumator1b_2_co), .co(co), .s(D3));
  not not_1 (not_1_out, b3);
  sumator1b sumator1b_2 (.a(a2), .b(not_2_out), .ci(sumator1b_3_co), .co(sumator1b_2_co), .s(D2));
  not not_2 (not_2_out, b2);
  sumator1b sumator1b_3 (.a(a1), .b(not_3_out), .ci(sumator1b_4_co), .co(sumator1b_3_co), .s(D1));
  not not_3 (not_3_out, b1);
  sumator1b sumator1b_4 (.a(a0), .b(not_4_out), .ci(Cin), .co(sumator1b_4_co), .s(D0));
  not not_4 (not_4_out, b0);
  depasire depasire_1 (.A3(a3), .B3(b3), .D3(D3), .ov(ov));

  // Notes on the sheet:
  //   Circuit depasire
endmodule

module sumator1b (
  input  a,
  input  b,
  input  ci,
  output co,
  output s
);

  wire demultiplexer_1_out0, demultiplexer_1_out1, demultiplexer_1_out2, demultiplexer_1_out3,
       demultiplexer_1_out4, demultiplexer_1_out5, demultiplexer_1_out6, demultiplexer_1_out7;

  Demultiplexer #(.select(3), .enable("false")) demultiplexer_1 (
    .out0(demultiplexer_1_out0), .out1(demultiplexer_1_out1), .out2(demultiplexer_1_out2),
    .out3(demultiplexer_1_out3), .out4(demultiplexer_1_out4), .out5(demultiplexer_1_out5),
    .out6(demultiplexer_1_out6), .out7(demultiplexer_1_out7), .in(1'b1), .sel({a, b, ci}));
  or or_1 (co, demultiplexer_1_out3, demultiplexer_1_out5, demultiplexer_1_out6, demultiplexer_1_out7);
  or or_2 (s, demultiplexer_1_out1, demultiplexer_1_out2, demultiplexer_1_out4, demultiplexer_1_out7);
endmodule

module depasire (
  input  A3,
  input  B3,
  input  D3,
  output ov
);

  Multiplexer #(.select(3), .enable("false")) multiplexer_1 (
    .in0(1'b0), .in1(1'b0), .in2(1'b0), .in3(1'b1), .in4(1'b1), .in5(1'b0), .in6(1'b0), .in7(1'b0), .out(ov),
    .sel({A3, B3, D3}));
endmodule
