// Logisim project Inmultire_Optim.circ as structural Verilog: 3 circuits, main circuit main
module main (
  input  SI,
  input  CLK,
  input  S_L,
  input  D3,
  input  D2,
  input  D1,
  input  D0,
  output Q3,
  output Q2,
  output Q1,
  output Q0
);

  wire multiplexer_1_out, multiplexer_2_out, multiplexer_3_out, multiplexer_4_out;

  Multiplexer #(.enable("false")) multiplexer_1 (.in0(D3), .in1(SI), .out(multiplexer_1_out), .sel(S_L));
  D_Flip_Flop d_ff_1 (.clk(CLK), .D(multiplexer_1_out), .Q(Q3));  // open: Qn, preset, en, reset
  Multiplexer #(.enable("false")) multiplexer_2 (.in0(D2), .in1(Q3), .out(multiplexer_2_out), .sel(S_L));
  D_Flip_Flop d_ff_2 (.clk(CLK), .D(multiplexer_2_out), .Q(Q2));  // open: Qn, preset, en, reset
  D_Flip_Flop d_ff_3 (.clk(CLK), .D(multiplexer_3_out), .Q(Q1));  // open: Qn, preset, en, reset
  Multiplexer #(.enable("false")) multiplexer_3 (.in0(D1), .in1(Q2), .out(multiplexer_3_out), .sel(S_L));
  Multiplexer #(.enable("false")) multiplexer_4 (.in0(D0), .in1(Q1), .out(multiplexer_4_out), .sel(S_L));
  D_Flip_Flop d_ff_4 (.clk(CLK), .D(multiplexer_4_out), .Q(Q0));  // open: Qn, preset, en, reset

  // Notes on the sheet:
  //   Registru serie-paralel
  //   S/L = 0 - incarcare paralela
  //   S/L = 1 - deplasare seriala la dreapta
endmodule

module inmultire (
  input  SL30,
  input  SL74,
  input  B3,
  input  B2,
  input  B1,
  input  B0,
  input  [3:0] A,
  input  RESET,
  output [3:0] P74,
  output [3:0] P30
);

  wire adder_1_cout, CLK30_out, CLK74_out, CLK_Cy_out, resetcy_1_q;
  wire [3:0] adder_1_out;

  Button CLK74 (.out(CLK74_out));
  Adder #(.width(4)) adder_1 (.a(P74), .b(A), .out(adder_1_out), .cout(adder_1_cout));  // open: cin
  Button CLK_Cy (.out(CLK_Cy_out));
  main main_1 (
    .SI(resetcy_1_q), .CLK(CLK74_out), .S_L(SL74), .Q3(P74[3]), .Q2(P74[2]), .Q1(P74[1]), .Q0(P74[0]),
    .D3(adder_1_out[3]), .D2(adder_1_out[2]), .D1(adder_1_out[1]), .D0(adder_1_out[0]));
  resetCy resetcy_1 (.CLK_Cy(CLK_Cy_out), .Cy(adder_1_cout), .RESET(RESET), .q(resetcy_1_q));
  Button CLK30 (.out(CLK30_out));
  main main_2 (
    .SI(P74[0]), .CLK(CLK30_out), .S_L(SL30), .Q3(P30[3]), .Q2(P30[2]), .Q1(P30[1]), .Q0(P30[0]), .D3(B3),
    .D2(B2), .D1(B1), .D0(B0));
endmodule

module resetCy (
  input  CLK_Cy,
  input  Cy,
  input  RESET,
  output q
);

  wire multiplexer_1_out;

  Multiplexer #(.enable("false")) multiplexer_1 (.in0(Cy), .in1(1'b0), .out(multiplexer_1_out), .sel(RESET));
  D_Flip_Flop d_ff_1 (.clk(CLK_Cy), .D(multiplexer_1_out), .Q(q));  // open: Qn, preset, en, reset
endmodule
