// Logisim project Impartirea.circ as structural Verilog: 3 circuits, main circuit ACC_ROM
module ACC_ROM (
  input  C2,
  input  C3,
  input  C4,
  input  C5,
  input  C6,
  input  D3,
  input  D2,
  input  D1,
  input  D0,
  input  I3,
  input  I2,
  input  I1,
  input  I0,
  output F6,
  output [3:0] out_15,
  output [3:0] out_16
);

  wire CLK_out, d_ff_1_qn, multiplexer_1_out, not_1_out, not_2_out;
  wire [2:0] counter_2_q;
  wire [3:0] counter_1_q, subtractor_1_out;
  wire [5:0] register_1_q;
  wire [7:0] rom_1_data;

  not not_1 (not_1_out, multiplexer_1_out);
  Counter #(.width(4), .max('hf)) counter_1 (
    .load(multiplexer_1_out), .D(rom_1_data[3:0]), .count(not_1_out), .Q(counter_1_q), .clk(CLK_out));  // open: carry, clr
  Button CLK (.out(CLK_out));
  Multiplexer #(.select(3), .disabled(0)) multiplexer_1 (
    .in0(subtractor_1_out[3]), .in1(counter_2_q[2]), .in2(C2), .in3(C3), .in4(C4), .in5(C5), .in6(C6),
    .in7(1'b1), .out(multiplexer_1_out), .sel(rom_1_data[6:4]), .en(not_2_out));
  ROM #(.addrWidth(4)) rom_1 (.addr(counter_1_q), .data(rom_1_data));  // open: sel
  not not_2 (not_2_out, rom_1_data[7]);
  Register #(.width(7)) register_1 (
    .D(rom_1_data[6:0]), .en(rom_1_data[7]), .Q({F6, register_1_q}), .clk(CLK_out));  // open: clr
  Subtractor #(.width(4)) subtractor_1 (.a(out_16), .b({I3, I2, I1, I0}), .out(subtractor_1_out));  // open: bin, bout
  RPS_Stanga rps_stanga_1 (
    .CLK(register_1_q[1]), .S_L(register_1_q[0]), .SI(out_15[3]), .O3(out_16[3]), .O2(out_16[2]),
    .O1(out_16[1]), .O0(out_16[0]), .I3(subtractor_1_out[3]), .I2(subtractor_1_out[2]),
    .I1(subtractor_1_out[1]), .I0(subtractor_1_out[0]));
  Counter #(.width(3), .max('h7)) counter_2 (
    .Q(counter_2_q), .clk(register_1_q[5]));  // open: load, D, count, carry, clr
  RPS_Stanga rps_stanga_2 (
    .CLK(register_1_q[3]), .S_L(register_1_q[2]), .SI(d_ff_1_qn), .O3(out_15[3]), .O2(out_15[2]),
    .O1(out_15[1]), .O0(out_15[0]), .I3(D3), .I2(D2), .I1(D1), .I0(D0));
  D_Flip_Flop d_ff_1 (.clk(register_1_q[4]), .D(subtractor_1_out[3]), .Qn(d_ff_1_qn));  // open: Q, preset, en, reset

  // Notes on the sheet:
  //   Program counter
  //   Memorie program - ROM
  //   contents of rom_1 (hex, n*v repeats v):
  //   80 88 85 8f 80 90 9 80 82 80 a0 1d 72 84 8c 7f
  //   Registru iesiri
endmodule

module main (
  input  S_L,
  input  S_L_2,
  input  D3,
  input  D2,
  input  D1,
  input  D0,
  input  I3,
  input  I2,
  input  I1,
  input  I0,
  output [3:0] out_11,
  output [3:0] out_12
);

  wire CLK_Cat_out, CLK_Rest_out, CLK_Semn_out, d_ff_1_qn;
  wire [3:0] subtractor_1_out;

  Button CLK_Rest (.out(CLK_Rest_out));
  RPS_Stanga rps_stanga_1 (
    .CLK(CLK_Rest_out), .S_L(S_L), .SI(out_12[3]), .O3(out_11[3]), .O2(out_11[2]), .O1(out_11[1]),
    .O0(out_11[0]), .I3(subtractor_1_out[3]), .I2(subtractor_1_out[2]), .I1(subtractor_1_out[1]),
    .I0(subtractor_1_out[0]));
  Subtractor #(.width(4)) subtractor_1 (.a(out_11), .b({I3, I2, I1, I0}), .out(subtractor_1_out));  // open: bin, bout
  Button CLK_Cat (.out(CLK_Cat_out));
  RPS_Stanga rps_stanga_2 (
    .CLK(CLK_Cat_out), .S_L(S_L_2), .SI(d_ff_1_qn), .O3(out_12[3]), .O2(out_12[2]), .O1(out_12[1]),
    .O0(out_12[0]), .I3(D3), .I2(D2), .I1(D1), .I0(D0));
  Button CLK_Semn (.out(CLK_Semn_out));
  D_Flip_Flop d_ff_1 (.clk(CLK_Semn_out), .D(subtractor_1_out[3]), .Qn(d_ff_1_qn));  // open: Q, preset, en, reset
endmodule

module RPS_Stanga (
  input  CLK,
  input  S_L,
  input  I3,
  input  I2,
  input  I1,
  input  I0,
  input  SI,
  output O3,
  output O2,
  output O1,
  output O0
);

  wire multiplexer_1_out, multiplexer_2_out, multiplexer_3_out, multiplexer_4_out;

  Multiplexer #(.enable("false")) multiplexer_1 (.in0(I3), .in1(O2), .out(multiplexer_1_out), .sel(S_L));
  D_Flip_Flop d_ff_1 (.clk(CLK), .D(multiplexer_1_out), .Q(O3));  // open: Qn, preset, en, reset
  Multiplexer #(.enable("false")) multiplexer_2 (.in0(I2), .in1(O1), .out(multiplexer_2_out), .sel(S_L));
  D_Flip_Flop d_ff_2 (.clk(CLK), .D(multiplexer_2_out), .Q(O2));  // open: Qn, preset, en, reset
  Multiplexer #(.enable("false")) multiplexer_3 (.in0(I1), .in1(O0), .out(multiplexer_3_out), .sel(S_L));
  D_Flip_Flop d_ff_3 (.clk(CLK), .D(multiplexer_3_out), .Q(O1));  // open: Qn, preset, en, reset
  D_Flip_Flop d_ff_4 (.clk(CLK), .D(multiplexer_4_out), .Q(O0));  // open: Qn, preset, en, reset
  Multiplexer #(.enable("false")) multiplexer_4 (.in0(I0), .in1(SI), .out(multiplexer_4_out), .sel(S_L));
endmodule
