// Logisim project ACC_ROM.circ as structural Verilog: 1 circuit, main circuit main
module main (
  input  C0,
  input  C1,
  input  C2,
  input  C3,
  input  C4,
  input  C5,
  input  C6,
  output F0,
  output F1,
  output F2,
  output F3,
  output F4,
  output F5,
  output F6
);

  wire CLK_out, multiplexer_1_out, not_1_out, not_2_out;
  wire [2:0] rom_1_data_2;
  wire [3:0] counter_1_q;
  wire [7:0] rom_1_data;

  not not_1 (not_1_out, multiplexer_1_out);
  Button CLK (.out(CLK_out));
  Counter #(.width(4), .max('hf)) counter_1 (
    .load(multiplexer_1_out), .D(rom_1_data[3:0]), .count(not_1_out), .Q(counter_1_q), .clk(CLK_out));  // open: carry, clr
  Multiplexer #(.select(3), .disabled(0)) multiplexer_1 (
    .in0(C0), .in1(C1), .in2(C2), .in3(C3), .in4(C4), .in5(C5), .in6(C6), .in7(1'b1),
    .out(multiplexer_1_out), .sel(rom_1_data_2), .en(not_2_out));
  ROM #(.addrWidth(4)) rom_1 (.addr(counter_1_q), .data({rom_1_data[7], rom_1_data_2, rom_1_data[3:0]}));  // open: sel
  Hex_Digit_Display hex_digit_display_1 (.value({1'b0, F6, F5, F4}));  // open: dp
  not not_2 (not_2_out, rom_1_data[7]);
  Hex_Digit_Display hex_digit_display_2 (.value({F3, F2, F1, F0}));  // open: dp
  Register #(.width(7)) register_1 (
    .D({rom_1_data_2, rom_1_data[3:0]}), .en(rom_1_data[7]), .Q({F6, F5, F4, F3, F2, F1, F0}), .clk(CLK_out));  // open: clr

  // Notes on the sheet:
  //   Program counter
  //   Memorie program - ROM
  //   contents of rom_1 (hex, n*v repeats v):
  //   b7 34 82 75 81 61 f3 77
  //   Registru iesiri
endmodule
